# Fritzing sketch projeto_final_fritzing (saved by Fritzing 0.9.3b)
circuit board: 7.42134cm x 5.8614cm
breadboards: 1

parts:
  J1 = Basic Servo
  J2 = Piezo Speaker
  R1 = Resistor [tolerance=±5% resistance=220 package=THT]
  R2 = Resistor [tolerance=±5% resistance=220 package=THT]
  LED3 = LED - 5mm [color="Red (633nm)" package="5 mm [THT]"]
  LED4 = LED - 5mm [color="Blue (525nm)" package="5 mm [THT]"]
  Componente2 = RFID USB Reader
  Componente1 = Arduino Uno (Rev3)

nets:
  GND: J1.gnd, J2.pin1, LED3.cathode, LED4.cathode, Componente2.TX-O, Componente1.GND
  VCC: J1.vcc, J1.pulse, Componente1.D6_PWM, Componente1.5V
  N1: J2.pin2, Componente1.D5_PWM
  N2: R1.Pin_0, Componente1.D2
  N3: R1.Pin_1, LED3.anode
  N4: R2.Pin_0, Componente1.D4
  N5: R2.Pin_1, LED4.anode
  N6: Componente2.GNDT, Componente1.D10_PWM/SS
  N7: Componente2.CP, Componente1.D13/SCK
  N8: Componente2.ANT2, Componente1.D11_PWM/MOSI
  N9: Componente2.ANT1, Componente1.D12/MISO
  N10: Componente2.GND, Componente1.D9_PWM
  VCC_2: Componente2.VCC, Componente1.3V3
